# Fritzing sketch SanguinoBB (saved by Fritzing 0.7.5b)
breadboards: 1

parts:
  Arduino2 = Arduino
  XTAL1 = Crystal [frequency="16 Mhz" package=THT]
  Part1 = FTDI Basic Programmer
  Atmega1 = ATmega644 [package=pdpi]
  S2 = Pushbutton [package="[THT]"]
  C1 = Ceramic Capacitor [capacitance=20pF package="200 mil [THT, multilayer]"]
  C2 = Ceramic Capacitor [capacitance=20pF package="200 mil [THT, multilayer]"]
  R1 = Resistor [tolerance=±5% resistance=10k package=THT]
  R2 = Resistor [tolerance=±5% resistance=1k package=THT]
  LED1 = LED - 3mm [color="Red (633nm)" package="3 mm [THT]"]

nets:
  N1: Arduino2.+5V, Atmega1.AVCC, Atmega1.AREF
  N2: Arduino2.GND, Atmega1.RESET, Atmega1.GND#30, S2.Pin_1, S2.Pin_2, S2.Pin_3, S2.Pin_4, R1.Pin_1, LED1.cathode
  N3: XTAL1.pin_0, Atmega1.XTAL1, C2.1
  N4: XTAL1.pin_1, Atmega1.XTAL2, C1.0
  N5: Part1.RXI, Atmega1.PD1
  N6: Part1.TXO, Atmega1.PD0
  N7: Part1.GND, C1.1, C2.0
  N8: Atmega1.PB0, R2.Pin_1
  N9: Atmega1.VCC, R1.Pin_0
  N10: R2.Pin_0, LED1.anode
